# Fritzing sketch arduino-yun-dashboard (saved by Fritzing 0.9.2b)
breadboards: 1

parts:
  Part1 = Base Shield V2
  Grove1 = Grove Temperature Sensor
  Grove2 = Grove Light Sensor
  Grove3 = Grove Rotary Angle Sensor
  LED1 = LED - 5mm [color="Red (633nm)" package="5 mm [THT]"]
  LED2 = LED - 5mm [color="Green (560nm)" package="5 mm [THT]"]
  LED3 = LED - 5mm [color="Yellow (585nm)" package="5 mm [THT]"]
  R1 = Resistor [tolerance=±5% resistance=1k package=THT]
  R2 = Resistor [tolerance=±5% resistance=1k package=THT]
  R3 = Resistor [tolerance=±5% resistance=1k package=THT]
  Part2 = SRF05 Ultrasonic Rangefinder

nets:
  N1: Part1.D9, LED3.anode
  N2: Part1.D10, LED2.anode
  N3: Part1.D11, LED1.anode
  N4: Part1.D12, Part2.Echo
  N5: Part1.D13, Part2.Trig
  5V: Part1.5V, Part2.VCC
  GND: Part1.GND, R1.Pin_1, R2.Pin_1, R3.Pin_1, Part2.GND
  N6: Part1.pin_140, Grove3.SIG
  N7: Part1.pin_142, Grove3.VCC
  N8: Part1.pin_143, Grove3.GND
  N9: Part1.pin_144, Grove1.SIG
  N10: Part1.pin_146, Grove1.VCC
  N11: Part1.pin_147, Grove1.GND
  N12: Part1.pin_148, Grove2.SIG
  N13: Part1.pin_150, Grove2.VCC
  N14: Part1.pin_151, Grove2.GND
  N15: LED1.cathode, R1.Pin_0
  N16: LED2.cathode, R2.Pin_0
  N17: LED3.cathode, R3.Pin_0

custom parts:
  Grove Rotary Angle Sensor: A potentiometer
